# Fritzing sketch Bluetooth controlled car (saved by Fritzing 0.9.3b)

parts:
  S1 = Toggle Switch [package=THT]
  R1 = Resistor [tolerance=±5% resistance=220 package="0603 [SMD]"]
  U1 = ESP32-38PinWide [part_number=ESP32-38PinWide]
  U2 = LIPO-110mAh [package=lipo-110]
  M1 = MT3608 Module
  Composant2 = Thumb Joystick
  Composant1 = Thumb Joystick
  LED1 = LED - 3mm [color="Red (633nm)" package="3 mm [THT]"]
  S3 = Toggle Switch [package=THT]
  C1 = Ceramic Capacitor [capacitance=100nF package="100 mil [THT, multilayer]"]
  M4 = MT3608 Module
  IC1 = L293D [package=THT]
  M3 = DC Motor
  U3 = ESP32-38PinWide [part_number=ESP32-38PinWide]
  M2 = DC Motor
  C2 = Ceramic Capacitor [capacitance=100nF package="100 mil [THT, multilayer]"]
  VCC1 = Battery block 9V
  U5 = LIPO-110mAh [package=lipo-110]

nets:
  N1: S1.COM, M1.pin2
  N2: S1.L2, U2.+
  N3: R1.Pin_0, U1.GPIO4
  N4: U1.GPIO26, Composant2.VERT
  N5: U1.GPIO27, Composant2.HORZ
  N6: U1.GPIO14, Composant1.VERT
  N7: U1.GPIO12, Composant1.HORZ
  GND: U1.GPIO11, M1.pin4, Composant2.GND, Composant1.GND, LED1.cathode
  VCC: U1.VIN, M1.pin3, Composant2.VCC, Composant1.VCC
  N8: U2.-, M1.pin1
  N9: S3.L1, M4.pin2
  N10: S3.COM, U5.+
  N11: C1.0, IC1.Out_1_(_Controlled_by_Enable_1_), M2.pin_1
  N12: C1.1, IC1.Out_2_(_Controlled_by_Enable_1_), M2.pin_2
  N13: M4.pin1, U5.-
  N14: M4.pin3, IC1.+V, U3.VIN
  N15: M4.pin4, IC1.0V, U3.GPIO11, VCC1.-
  N16: IC1.Enable_1, U3.GPIO25
  N17: IC1.In_1, U3.GPIO33
  N18: IC1.In_2, U3.GPIO32
  N19: IC1.+Vmotor, VCC1.+
  N20: IC1.Enable_2, U3.GPIO26
  N21: IC1.In_3, U3.GPIO14, U3.GPIO12
  N22: IC1.Out_3_(_Controlled_by_Enable_2_), M3.pin_2, C2.0
  N23: IC1.Out_4_(_Controlled_by_Enable_2_), M3.pin_1, C2.1
  N24: IC1.In_4, U3.GPIO27

custom parts:
  ESP32-38PinWide: Generic 38-Pin ESP32 with wide format (only access to one side of pins on a breadboard) based on Stephen Lilley's HiLetgo ESP-WROOM-32 ESP32 ESP-32S Development Board.
  MT3608 Module: MT3608 Boost Converter Module Links: Aerosemi MT3608 2A Step Up Converter datasheet
